// Digital circuit RISCV.dig as structural Verilog
module RISCV (
  input  [31:0] in_1,
  input  [31:0] in_2,
  input  in_3,
  input  [31:0] in_5,
  input  [31:0] in_6,
  input  [31:0] in_8,
  input  [1:0] in_9,
  input  [31:0] in_10,
  input  [31:0] in_11,
  input  [1:0] in_12,
  input  [4:0] in_15,
  input  [4:0] in_16,
  input  in_17,
  input  in_18,
  input  [4:0] in_19,
  input  [31:0] in_20,
  input  in_23,
  input  [31:0] in_28,
  input  in_29,
  input  [31:0] in_30,
  output [31:0] out_4,
  output [31:0] out_7,
  output out_13,
  output [31:0] out_14,
  output [31:0] out_21,
  output [31:0] out_22,
  output [6:0] out_24,
  output [4:0] out_25,
  output [4:0] out_26,
  output [4:0] out_27,
  output [31:0] out_31
);

  ALU #(.applicationType("GHDL")) u_ALU (.A(in_10), .B(in_11), .selector(in_12), .Zero(out_13), .Result(out_14));
  MUX_2inputs #(.applicationType("GHDL")) u_MUX_2inputs (
    .enter1(in_1), .enter2(in_2), .selector(in_3), .\output (out_4));
  MUX_3inputs #(.applicationType("GHDL")) u_MUX_3inputs (
    .enter1(in_5), .enter2(in_6), .enter3(in_8), .selector(in_9), .\output (out_7));
  register_block #(.applicationType("GHDL")) u_register_block (
    .rg1(in_15), .rg2(in_16), .CLK(in_17), .reg_write(in_18), .rgw(in_19), .rgw_data(in_20),
    .rg1_data(out_21), .rg2_data(out_22));
  IR_block #(.applicationType("GHDL")) u_IR_block (
    .memData(in_28), .CLK(in_23), .opcode(out_24), .rs1(out_25), .rs2(out_26), .rd(out_27));
  memory_register #(.applicationType("GHDL")) u_memory_register (.memData(in_30), .CLK(in_29), .memOutput(out_31));
  output_control #(.applicationType("GHDL")) u_output_control ();  // open: opcode, IRWrite, MemtoReg, MemWrite, MemRead, IorD, PCWrite, PCWriteCond, PCSource, ALUOp, ALUSrcB, ALUSrcA, RegWrite
  output_control #(.applicationType("GHDL")) u_output_control_2 ();  // open: opcode, IRWrite, MemtoReg, MemWrite, MemRead, IorD, PCWrite, PCWriteCond, PCSource, ALUOp, ALUSrcB, ALUSrcA, RegWrite
endmodule

/* Code of ALU:
LIBRARY ieee;
USE ieee.std_logic_1164.all;
USE ieee.numeric_std.all;

ENTITY ALU IS
	PORT(
		A, B : IN STD_LOGIC_VECTOR(31 downto 0);
		selector : IN STD_LOGIC_VECTOR(1 downto 0);
        	Zero    : OUT STD_LOGIC;
		Result : OUT STD_LOGIC_VECTOR(31 downto 0)
	);
END ALU;

ARCHITECTURE ALU_logic OF ALU IS

	signal B_eff    : STD_LOGIC_VECTOR(31 downto 0);

	constant allZero : std_logic_vector(31 downto 0) := (others => '0');
	constant allOne : std_logic_vector(31 downto 0) := (others => '1');

    	signal Sum_ext  : UNSIGNED(32 downto 0);

    	signal Res_temp : STD_LOGIC_VECTOR(31 downto 0);
	signal and_temp : STD_LOGIC_VECTOR(31 downto 0);
	signal or_temp : STD_LOGIC_VECTOR(31 downto 0);

    	signal Cin_vec  : UNSIGNED(32 downto 0);

	BEGIN

		and_temp <= A AND B;
		or_temp <= A OR B;

------------------------------------

    B_eff <= (B xor allOne) WHEN (selector = "01") ELSE
		B;

    Cin_vec <= unsigned(allZero & selector(0));

    Sum_ext <= unsigned('0' & A) + unsigned('0' & B_eff) + Cin_vec;

    Res_temp <= std_logic_vector(Sum_ext(31 downto 0));

    Zero <= '1' WHEN ((Res_temp = allZero) AND (selector(1) = '0')) ELSE
		'0';

    Result <= and_temp WHEN (selector = "10") ELSE
		or_temp WHEN (selector = "11") ELSE
		Res_temp;

	END ALU_logic;
*/

/* Code of MUX_2inputs:
LIBRARY ieee;
USE ieee.std_logic_1164.all;

ENTITY MUX_2inputs IS
	PORT(
		enter1, enter2 : IN STD_LOGIC_VECTOR (31 downto 0);
		selector : IN STD_LOGIC;
		output : OUT STD_LOGIC_VECTOR (31 downto 0)
	);
END MUX_2inputs;

ARCHITECTURE MUX_logic OF MUX_2inputs IS
	BEGIN
		output <= enter1 WHEN selector = '0' ELSE
			enter2;

	END MUX_logic;
--------------------------------------------------------------------------------
*/

/* Code of MUX_3inputs:
LIBRARY ieee;
USE ieee.std_logic_1164.all;

ENTITY MUX_3inputs IS
	PORT(
		enter1, enter2, enter3 : IN STD_LOGIC_VECTOR (31 downto 0);
		selector: IN STD_LOGIC_VECTOR (1 downto 0);
		output : OUT STD_LOGIC_VECTOR (31 downto 0)
	);
END MUX_3inputs;

ARCHITECTURE MUX_logic OF MUX_3inputs IS
	BEGIN
		output <= enter1 WHEN selector = "00" ELSE
			enter2 WHEN selector = "01" ELSE
			enter3;

	END MUX_logic;
--------------------------------------------------------------------------------
*/

/* Code of register_block:
LIBRARY ieee;
USE ieee.std_logic_1164.all;
USE ieee.numeric_std.all;

ENTITY register_block IS
	PORT(
		rg1, rg2 : IN STD_LOGIC_VECTOR(4 downto 0);
		CLK : IN STD_LOGIC;
		reg_write : IN STD_LOGIC;
		rgw : IN STD_LOGIC_VECTOR(4 downto 0);
		rgw_data : IN STD_LOGIC_VECTOR(31 downto 0);
		rg1_data , rg2_data : OUT STD_LOGIC_VECTOR(31 downto 0)
	);
END register_block;

ARCHITECTURE register_logic OF register_block IS

	type reg_array is array (0 to 31) of std_logic_vector(31 downto 0);
	signal registers : reg_array := (others => (others => '0'));
	signal value1 : STD_LOGIC_VECTOR(31 downto 0);
	signal value2 : STD_LOGIC_VECTOR(31 downto 0);

	BEGIN
	
		PROCESS(CLK)
			BEGIN
				IF (CLK'event AND CLK='1') THEN
					IF (reg_write = '1' AND rgw /= "00000") THEN
						registers(to_integer(unsigned(rgw))) <= rgw_data;
					END IF;
				END IF;
		END PROCESS;

		rg1_data <= registers(to_integer(unsigned(rg1)));
		rg2_data <= registers(to_integer(unsigned(rg2)));

	END register_logic;
*/

/* Code of IR_block:
LIBRARY ieee;
USE ieee.std_logic_1164.all;
USE ieee.numeric_std.all;

ENTITY IR_block IS
	PORT(
		memData : IN STD_LOGIC_VECTOR(31 downto 0);
		CLK : IN STD_LOGIC;
		opcode : OUT STD_LOGIC_VECTOR(6 downto 0);
		rs1 : OUT STD_LOGIC_VECTOR(4 downto 0);
		rs2 : OUT STD_LOGIC_VECTOR(4 downto 0);
		rd : OUT STD_LOGIC_VECTOR(4 downto 0)
	);
END IR_block;

ARCHITECTURE IR_logic OF IR_block IS
	BEGIN
	
		PROCESS(CLK)
			BEGIN
				IF (CLK'event AND CLK='1') THEN
					opcode <= memData(6 downto 0);
					rs1 <= memData(19 downto 15);
					rs2 <= memData(24 downto 20);
					rd <= memData(11 downto 7);
				ELSE
					opcode <= opcode;
					rs1 <= rs1;
					rs2 <= rs2;
					rd <= rd;
				END IF;
		END PROCESS;

	END IR_logic;
*/

/* Code of memory_register:
LIBRARY ieee;
USE ieee.std_logic_1164.all;
USE ieee.numeric_std.all;

ENTITY memory_register IS
	PORT(
		memData : IN STD_LOGIC_VECTOR(31 downto 0);
		CLK : IN STD_LOGIC;
		memOutput : OUT STD_LOGIC_VECTOR(31 downto 0)
	);
END memory_register;

ARCHITECTURE memory_register_logic OF memory_register IS
	BEGIN
	
		PROCESS(CLK)
			BEGIN
				IF (CLK'event AND CLK='1') THEN
					memOutput <= memData;
				ELSE
					memOutput <= memOutput;
				END IF;
		END PROCESS;

	END memory_register_logic;
*/

/* Code of output_control:
LIBRARY ieee;
USE ieee.std_logic_1164.all;
USE ieee.numeric_std.all;

ENTITY output_control IS
	PORT(
		opcode : IN STD_LOGIC_VECTOR(6 downto 0);
		IRWrite : OUT STD_LOGIC;
		MemtoReg : OUT STD_LOGIC;
		MemWrite : OUT STD_LOGIC;
		MemRead : OUT STD_LOGIC;
		IorD : OUT STD_LOGIC;
		PCWrite : OUT STD_LOGIC;
		PCWriteCond : OUT STD_LOGIC;
		PCSource : OUT STD_LOGIC;
		ALUOp : OUT STD_LOGIC;
		ALUSrcB : OUT STD_LOGIC_VECTOR (1 downto 0);
		ALUSrcA : OUT STD_LOGIC;
		RegWrite : OUT STD_LOGIC
	);
END output_control;

ARCHITECTURE output_control_logic OF output_control IS

	CONSTANT opAritmetica : STD_LOGIC_VECTOR(6 downto 0) := "0110011";
	CONSTANT opAritmeticaImm : STD_LOGIC_VECTOR(6 downto 0) := "0010011";
	CONSTANT LW : STD_LOGIC_VECTOR(6 downto 0) := "0000011";
	CONSTANT SW : STD_LOGIC_VECTOR(6 downto 0) := "0100011";
	CONSTANT LUI : STD_LOGIC_VECTOR(6 downto 0) := "0110111";
	CONSTANT AUIPC : STD_LOGIC_VECTOR(6 downto 0) := "0010111";
	CONSTANT JALR : STD_LOGIC_VECTOR(6 downto 0) := "1100111";
	CONSTANT JAL : STD_LOGIC_VECTOR(6 downto 0) := "1101111";
	CONSTANT BRANCH : STD_LOGIC_VECTOR(6 downto 0) := "1100111";

	BEGIN
		RegWrite <= '1' WHEN (opcode = opAritmetica OR opcode = opAritmeticaImm
			OR opcode = LW OR opcode = LUI OR opcode = JALR OR opcode = JAL) ELSE
			    '0';

		ALUSrcA <= '1' WHEN (opcode = opAritmetica OR opcode = opAritmeticaImm
			OR opcode = LW OR opcode = SW OR opcode = LUI OR opcode = BRANCH) ELSE
			    '0';

		ALUSrcB <= "00" WHEN (opcode = opAritmetica OR opcode = BRANCH) ELSE
			    "10" WHEN (opcode = opAritmeticaImm OR opcode = LW OR 
				opcode = LW OR opcode = LUI OR opcode = AUIPC OR opcode = JAL
				OR opcode = JALR) ELSE 
				"01";

	END output_control_logic;
*/
